# Fritzing sketch opto_can_feedback_8x_v1_rev5 (saved by Fritzing 0.9.3b)
circuit board: 8cm x 6.6cm
breadboards: 1

parts:
  RNW3 = male pin header, 8 pins [form="♂ (male)" part_number=Netzwerk]
  RNW4 = male pin header, 8 pins [form="♂ (male)" part_number=Netzwerk]
  OK1 = LTV 847 [part_number=LTV744 package="DIP (Dual Inline) [THT]"]
  OK2 = LTV 847 [part_number=LTV744 package="DIP (Dual Inline) [THT]"]
  RNW1 = male pin header, 8 pins [form="♂ (male)" part_number=Netzwerk]
  RNW2 = male pin header, 8 pins [form="♂ (male)" part_number=Netzwerk]
  D10 = Resistor [tolerance=±5% resistance=220 package=THT]
  D23 = Resistor [tolerance=±5% resistance=220 package=THT]
  D11 = Resistor [tolerance=±5% resistance=220 package=THT]
  D14 = Resistor [tolerance=±5% resistance=220 package=THT]
  D16 = Resistor [tolerance=±5% resistance=220 package=THT]
  D27 = Resistor [tolerance=±5% resistance=220 package=THT]
  D28 = Resistor [tolerance=±5% resistance=220 package=THT]
  D29 = Resistor [tolerance=±5% resistance=220 package=THT]
  MCP2515 = MCP2515 [package="DIP (Dual Inline) [THT]"]
  CAN2 = RJ45 Jack [package=rj45-8]
  C3 = Ceramic Capacitor [capacitance=100nF package="100 mil [THT, multilayer]"]
  C4 = Ceramic Capacitor [capacitance=100nF package="100 mil [THT, multilayer]"]
  R6 = Resistor [tolerance=±5% resistance=330 package=THT]
  ISO1050 = ISO1050 DUP [package="DIP (Dual Inline) [THT]"]
  CAN1 = RJ45 Jack [package=rj45-8]
  ATmega328 = atmega328 [package=dip]
  Clock = Crystal [frequency="16 Mhz" package=THT]
  C6 = Capacitor [part_number=22pf package=cap-pth-small2]
  C5 = Capacitor [part_number=22pf package=cap-pth-small2]
  C1 = Ceramic Capacitor [capacitance=100nF package="100 mil [THT, multilayer]"]
  C2 = Ceramic Capacitor [capacitance=100nF package="100 mil [THT, multilayer]"]
  R4 = Resistor [tolerance=±5% resistance=330 package=THT]
  R5 = Resistor [tolerance=±5% resistance=330 package=THT]
  R2 = Resistor [tolerance=±5% resistance=1k package=THT]
  USB_PWR = USB Connectors [package=usb-mb-h]
  LEDMSG = LED - 3mm [color="Orange (620nm)" package="3 mm [THT]"]
  R1 = Resistor [tolerance=±5% resistance=330 package=THT]
  Input2 = screw terminal, 4 pins
  Input = Screw terminal - 2 pins [package=THT]
  Input1 = screw terminal, 4 pins
  PortNr = IC, DIP package, 6 pins [chip_label=PortNr]
  7805 = Voltage Regulator - 5V [package="DPak [SMD]"]
  RESET = Pushbutton [package=THT]
  PRGBTN = Pushbutton [package=THT]
  CAN_ON = LED - 3mm [color="Red (633nm)" package="3 mm [THT]"]
  CPU = LED - 3mm [color="Green (570nm)" package="3 mm [THT]"]
  Power = LED - 3mm [color="Red (633nm)" package="3 mm [THT]"]
  ICSP = shrouded pin header, 6 pins [form="♂ (shrouded male)"]
  Clock_CAN = Crystal [frequency="16 Mhz" package=THT]
  C7 = Capacitor [part_number=22pf package=cap-pth-small2]
  J1 = male pin header, 2 pins [form="♂ (male)"]
  C8 = Capacitor [part_number=22pf package=cap-pth-small2]
  D1 = Resistor [tolerance=±5% resistance=220 package=THT]
  D2 = Resistor [tolerance=±5% resistance=220 package=THT]
  D3 = Resistor [tolerance=±5% resistance=220 package=THT]
  D4 = Resistor [tolerance=±5% resistance=220 package=THT]
  D34 = Resistor [tolerance=±5% resistance=220 package=THT]
  D35 = Resistor [tolerance=±5% resistance=220 package=THT]
  D8 = Resistor [tolerance=±5% resistance=220 package=THT]
  D37 = Resistor [tolerance=±5% resistance=220 package=THT]

nets:
  GND: RNW3.pin1, RNW3.pin3, RNW3.pin5, RNW3.pin7, RNW4.pin1, RNW4.pin3, RNW4.pin5, RNW4.pin7, MCP2515.VSS, ISO1050.GND1, ATmega328.GND, C6.2, C5.1, C1.0, C2.1, R4.Pin_0, R5.Pin_0, USB_PWR.GND, LEDMSG.cathode, PortNr.pin2, PortNr.pin5, RESET.leg1, PRGBTN.leg1, ICSP.pin4, C7.2, J1.pin2, C8.1
  N1: RNW3.pin2, OK2.Out4e, ATmega328.D7
  N2: RNW3.pin4, OK2.Out3e, ATmega328.D6_(PWM)
  N3: RNW3.pin6, OK2.Out2e, ATmega328.D5_(PWM)
  N4: RNW3.pin8, OK2.Out1e, ATmega328.D9_(PWM)
  N5: RNW4.pin2, OK1.Out4e, ATmega328.A0
  N6: RNW4.pin4, OK1.Out3e, ATmega328.A1
  N7: RNW4.pin6, OK1.Out2e, ATmega328.A2
  N8: RNW4.pin8, OK1.Out1e, ATmega328.A3
  N9: OK1.IN1a, RNW1.pin1, D14.Pin_0, D4.Pin_1
  N10: OK1.IN1c, OK1.IN2c, OK1.IN3c, OK1.IN4c, OK2.IN1c, OK2.IN2c, OK2.IN3c, OK2.IN4c, D10.Pin_1, D23.Pin_1, D11.Pin_1, D14.Pin_1, D16.Pin_1, D27.Pin_1, D28.Pin_1, D29.Pin_1, Input.pin1, Input.pin2, D1.Pin_0, D2.Pin_0, D3.Pin_0, D4.Pin_0, D34.Pin_0, D35.Pin_0, D8.Pin_0, D37.Pin_0
  N11: OK1.IN2a, RNW1.pin3, D11.Pin_0, D3.Pin_1
  N12: OK1.IN3a, RNW1.pin5, D23.Pin_0, D2.Pin_1
  N13: OK1.IN4a, RNW1.pin7, D10.Pin_0, D1.Pin_1
  VDD: OK1.Out1c, OK1.Out2c, OK1.Oute3c, OK1.Ou4c, OK2.Out1c, OK2.Out2c, OK2.Oute3c, OK2.Ou4c, MCP2515.VDD, ISO1050.Vcc1, ATmega328.VCC, ATmega328.AVCC, C1.1, C2.0, R2.Pin_0, USB_PWR.VBUS, Power.anode, ICSP.pin6
  N14: OK2.IN1a, RNW2.pin1, D28.Pin_0, D37.Pin_1
  N15: OK2.IN2a, RNW2.pin3, D16.Pin_0, D35.Pin_1
  N16: OK2.IN3a, RNW2.pin5, D29.Pin_0, D34.Pin_1
  N17: OK2.IN4a, RNW2.pin7, D27.Pin_0, D8.Pin_1
  N18: RNW1.pin2, Input1.pin4
  N19: RNW1.pin4, Input1.pin3
  N20: RNW1.pin6, Input1.pin2
  N21: RNW1.pin8, Input1.pin1
  N22: RNW2.pin2, Input2.pin4
  N23: RNW2.pin4, Input2.pin3
  N24: RNW2.pin6, Input2.pin2
  N25: RNW2.pin8, Input2.pin1
  N26: MCP2515.TXCAN, ISO1050.TXD
  N27: MCP2515.RXCAN, ISO1050.RXD
  N28: MCP2515.OSC2, Clock_CAN.pin_1, C7.1
  N29: MCP2515.OSC1, Clock_CAN.pin_0, C8.2
  N30: MCP2515.INT, ATmega328.D2
  N31: MCP2515.SCK, ATmega328.D13, CPU.anode, ICSP.pin2
  N32: MCP2515.SI, ATmega328.D11_(PWM), ICSP.pin5
  N33: MCP2515.SO, ATmega328.D12, ICSP.pin1
  N34: MCP2515.CS, ATmega328.D10_(PWM)
  N35: MCP2515.RESET, ATmega328.RESET, R2.Pin_1, RESET.leg0, ICSP.pin3
  N36: CAN2.1, CAN1.1
  N37: CAN2.2, CAN1.2
  GND2: CAN2.3, CAN2.4, C3.1, C4.0, R6.Pin_1, ISO1050.GND2, CAN1.3, CAN1.4, 7805.GND
  N38: CAN2.5, CAN2.6, C3.0, CAN1.5, CAN1.6, 7805.input_voltage
  N39: CAN2.7, ISO1050.CANL, CAN1.7
  N40: CAN2.8, ISO1050.CANH, CAN1.8
  N41: C4.1, ISO1050.Vcc2, 7805.output_voltage, CAN_ON.anode
  N42: R6.Pin_0, CAN_ON.cathode
  N43: ATmega328.D0_(RX), PortNr.pin1
  N44: ATmega328.D1_(TX), PortNr.pin3
  N45: ATmega328.D3_(PWM), PortNr.pin6
  N46: ATmega328.D4, PortNr.pin4
  N47: ATmega328.XLAT1, Clock.pin_0, C6.1
  N48: ATmega328.XLAT2, Clock.pin_1, C5.2
  N49: ATmega328.D8, J1.pin1
  N50: ATmega328.A4, R1.Pin_1
  N51: ATmega328.A5, PRGBTN.leg0
  N52: R4.Pin_1, Power.cathode
  N53: R5.Pin_1, CPU.cathode
  N54: LEDMSG.anode, R1.Pin_0

notes:
  (c)2017 mra@coraxium.de
  Opto Feedback 8x CAN Card rev5
  5  6  7  8
  1  2  3  4
  GND/0
  Vcc
  GND
  SI
  SO
  SCK
  RST
  --------------
  ------------------------
  Input
  ------
  -----
  --------
  1
  8
  2
  4

custom parts:
  LTV 847: 4xOK
  MCP2515: CAN-Controller
  ISO1050 DUP: Isolated CAN Transceiver
