# Fritzing sketch lichtschranke_km153p_platine (saved by Fritzing 0.9.2b)
circuit board: 5cm x 1.5cm
breadboards: 1

parts:
  J4 = male pin header, 3 pins [form="♂ (male)"]
  R3 = Resistor [tolerance=±5% resistance=100 package=THT]
  R4 = Resistor [tolerance=±5% resistance=10k package=THT]
  J6 = male pin header, 2 pins [form="♂ (male)"]
  J5 = male pin header, 2 pins [form="♂ (male)"]

nets:
  N1: J4.pin1, R3.Pin_1, R4.Pin_1
  N2: J4.pin2, R4.Pin_0, J5.pin2
  N3: J4.pin3, J6.pin2, J5.pin1
  N4: R3.Pin_0, J6.pin1

notes:
  d
  +
  c
  e
  mra@coraxium.de
  Gleis-Lichtschranke
  Sender
  A
  E
  +5V
  Data
  GND
  10k
  100
  TEMIC K153p
