# Fritzing sketch lichtschranke_steuerung_km153p_platine_DS_v3_rev.01 (saved by Fritzing 0.9.2b)
circuit board: 7.48353cm x 7.01314cm
breadboards: 1

parts:
  J4 = screw terminal, 8 pins
  J5 = Screw terminal - 2 pins [package=THT]
  D1 = Diode [package=diode-1n4001]
  C5 = Capacitor Polarized [package=cpol-radial-10uf-25v]
  J8 = longpad pin header, 2 pins [form="long pad"]
  BrGlr = IC, DIP package, 6 pins [chip_label=GL]
  RNW1 = male pin header, 8 pins [form="♂ (male)" part_number=Netzwerk]
  OK847-1 = IC, DIP package, 16 pins [chip_label=IC]
  OK847-2 = IC, DIP package, 16 pins [chip_label=IC]
  RNW2 = male pin header, 8 pins [form="♂ (male)" part_number=Netzwerk]
  J9 = screw terminal, 8 pins
  RESET = Pushbutton [package="[THT]"]
  J10 = female pin header, 3 pins [form="♀ (female)"]
  J11 = female pin header, 4 pins [form="♀ (female)"]
  C7 = Ceramic Capacitor [capacitance="100 nF" package="100 mil [THT, multilayer]"]
  C8 = Ceramic Capacitor [capacitance="100 nF" package="100 mil [THT, multilayer]"]
  J14 = female pin header, 3 pins [form="♀ (female)"]
  J15 = female pin header, 3 pins [form="♀ (female)"]
  7805 = Voltage Regulator - Variable [part_number=7805 package="TO220 [THT]"]
  J7 = Screw terminal - 2 pins [package=THT]
  J6 = Screw terminal - 2 pins [package=THT]
  Arduino_Nano = Arduino Nano (Rev3.0) (ICSP)
  J17 = female pin header, 4 pins [form="♀ (female)"]
  RNW3 = male pin header, 8 pins [form="♂ (male)" part_number=Netzwerk]
  RNW4 = male pin header, 8 pins [form="♂ (male)" part_number=Netzwerk]
  J18 = female pin header, 2 pins [form="♀ (female)"]
  J19 = Screw terminal - 2 pins [package=THT]
  J12 = female pin header, 2 pins [form="♀ (female)"]
  J16 = female pin header, 4 pins [form="♀ (female)"]
  J20 = Screw terminal - 2 pins [package=THT]

nets:
  N1: J4.pin1, OK847-2.pin16
  N2: J4.pin2, OK847-2.pin14
  N3: J4.pin3, OK847-2.pin12
  N4: J4.pin4, OK847-2.pin10
  N5: J4.pin5, OK847-1.pin16
  N6: J4.pin6, OK847-1.pin14
  N7: J4.pin7, OK847-1.pin12
  N8: J4.pin8, OK847-1.pin10
  N9: J5.pin1, J5.pin2, OK847-1.pin9, OK847-1.pin11, OK847-1.pin13, OK847-1.pin15, OK847-2.pin9, OK847-2.pin11, OK847-2.pin13, OK847-2.pin15
  N10: D1.A, BrGlr.pin1, J6.pin1
  N11: D1.C, C5.+, C7.0, 7805.ADJ
  N12: C5.-, J8.pin2, BrGlr.pin3, RNW1.pin1, RNW1.pin3, RNW1.pin5, RNW1.pin7, RNW2.pin1, RNW2.pin3, RNW2.pin5, RNW2.pin7, RESET.Pin_1, RESET.Pin_2, C7.1, C8.1, J14.pin1, J14.pin2, J14.pin3, J15.pin1, J15.pin2, J15.pin3, 7805.OUT, J6.pin2, Arduino_Nano.GND, J17.pin1, J17.pin2, J17.pin3, J17.pin4, RNW3.pin1, RNW3.pin3, RNW3.pin5, RNW3.pin7, RNW4.pin1, RNW4.pin3, RNW4.pin5, RNW4.pin7, J18.pin1, J19.pin2, J20.pin2
  N13: J8.pin1, J11.pin1, Arduino_Nano.5V, J18.pin2, J19.pin1, J16.pin1, J16.pin2, J16.pin3, J16.pin4, J20.pin1
  N14: BrGlr.pin4, J7.pin1
  N15: BrGlr.pin6, J7.pin2
  N16: RNW1.pin2, OK847-1.pin2
  N17: RNW1.pin4, OK847-1.pin4
  N18: RNW1.pin6, OK847-1.pin6
  N19: RNW1.pin8, OK847-1.pin8
  N20: OK847-1.pin1, Arduino_Nano.A0
  N21: OK847-1.pin3, Arduino_Nano.D12/MISO
  N22: OK847-1.pin5, Arduino_Nano.D11/MOSI
  N23: OK847-1.pin7, Arduino_Nano.D10
  N24: OK847-2.pin1, Arduino_Nano.A4
  N25: OK847-2.pin2, RNW2.pin2
  N26: OK847-2.pin3, Arduino_Nano.A3
  N27: OK847-2.pin4, RNW2.pin4
  N28: OK847-2.pin5, Arduino_Nano.A2
  N29: OK847-2.pin6, RNW2.pin6
  N30: OK847-2.pin7, Arduino_Nano.A1
  N31: OK847-2.pin8, RNW2.pin8
  N32: J9.pin1, Arduino_Nano.D2, RNW4.pin2
  N33: J9.pin2, Arduino_Nano.D3, RNW4.pin4
  N34: J9.pin3, Arduino_Nano.D4, RNW4.pin6
  N35: J9.pin4, Arduino_Nano.D5, RNW4.pin8
  N36: J9.pin5, Arduino_Nano.D6, RNW3.pin2
  N37: J9.pin6, Arduino_Nano.D7, RNW3.pin4
  N38: J9.pin7, Arduino_Nano.D8, RNW3.pin6
  N39: J9.pin8, Arduino_Nano.D9, RNW3.pin8
  N40: RESET.Pin_3, RESET.Pin_4, Arduino_Nano.RESET
  N41: J10.pin1, Arduino_Nano.AREF
  N42: J10.pin2, Arduino_Nano.3V3
  N43: J10.pin3, Arduino_Nano.D13/SCK
  N44: J11.pin2, Arduino_Nano.A7
  N45: J11.pin3, Arduino_Nano.A6
  N46: J11.pin4, Arduino_Nano.A5
  N47: C8.0, 7805.IN
  N48: Arduino_Nano.D1/TX, J12.pin2
  N49: Arduino_Nano.D0/RX, J12.pin1

notes:
  d
  +
  c
  e
  --------------------------------
  mra@coraxium.de
  Rev. 01
  Controller Lichtschranken 3
  GND
  8
  1
  OUT
  IN
  7-12V=
  5V+
  Rx/Tx
  AC 16V
  GND  5V
  5V GND
  Reset
