# Fritzing sketch automatic_lighting_v3_wo_smd (saved by Fritzing 0.9.3b)
circuit board: 3.95053cm x 2.3501cm
breadboards: 1

parts:
  J3 = Generic double row male header - 6 pins [form="♂ (male)" package=THT]
  ATTiny85 = ATTINY45 [package=so]
  S1 = Pushbutton [package=THT]
  S2 = Pushbutton [package=THT]
  DC_5V = Screw terminal - 2 pins [package=THT]
  K- = screw terminal, 6 pins
  A+ = screw terminal, 6 pins
  R1 = Resistor [tolerance=±5% resistance=10k package=THT]
  R2 = Resistor [tolerance=±5% resistance=10k package=THT]
  R5 = Resistor [tolerance=±5% resistance=330 package=THT]
  R6 = Resistor [tolerance=±5% resistance=330 package=THT]
  R7 = Resistor [tolerance=±5% resistance=330 package=THT]

nets:
  N1: J3.MISO, ATTiny85.PB1(MISO), R6.Pin_1
  N2: J3.SCK, ATTiny85.PB2(SCK_ADC1), R7.Pin_0
  N3: J3.^RESET, ATTiny85.PB5(NRES)
  GND: J3.GND, ATTiny85.GND, S1.leg0, S2.leg0, DC_5V.pin1
  N4: J3.MOSI, ATTiny85.PB0(MOSI), R5.Pin_1
  5V: J3.5V, ATTiny85.VCC, DC_5V.pin2, R1.Pin_1, R2.Pin_0
  N5: ATTiny85.PB3(ADC3), S1.leg1, R1.Pin_0
  N6: ATTiny85.PB4(ADC2), S2.leg1, R2.Pin_1
  N7: K-.pin1, K-.pin5, A+.pin2, A+.pin6, R7.Pin_1
  N8: K-.pin2, K-.pin4, A+.pin1, A+.pin3, R5.Pin_0
  N9: K-.pin3, K-.pin6, A+.pin4, A+.pin5, R6.Pin_0

notes:
  GND
  Vcc
  MISO
  SCK
  Rev.3
  RESET
  ICSP
  (c) 2017 mra@coraxium.de
  Lichtprozessor 3X6
  MOSI

custom parts:
  Generic double row male header - 6 pins: Generic double row male header
