# Fritzing sketch automatic_lighting_v4_Doppelstock_wo_smd (saved by Fritzing 0.9.3b)
circuit board: 4.5cm x 2.4cm
breadboards: 1

parts:
  J3 = Generic double row male header - 6 pins [form="♂ (male)" package=THT]
  ATTiny85 = ATTINY45 [package=so]
  S1 = Pushbutton [package=THT]
  S2 = Pushbutton [package=THT]
  DC_5V = Screw terminal - 2 pins [package=THT]
  K- = screw terminal, 6 pins
  R1 = Resistor [tolerance=±5% resistance=10k package=THT]
  R2 = Resistor [tolerance=±5% resistance=10k package=THT]
  R4 = Resistor [tolerance=±5% resistance=330 package=THT]
  R5 = Resistor [tolerance=±5% resistance=330 package=THT]
  R3 = Resistor [tolerance=±5% resistance=330 package=THT]
  A+1 = screw terminal, 6 pins

nets:
  N1: J3.MISO, ATTiny85.PB1(MISO), R4.Pin_0
  N2: J3.SCK, ATTiny85.PB2(SCK_ADC1), R5.Pin_0
  N3: J3.^RESET, ATTiny85.PB5(NRES)
  GND: J3.GND, ATTiny85.GND, S1.leg0, S2.leg0, DC_5V.pin1
  N4: J3.MOSI, ATTiny85.PB0(MOSI), R3.Pin_0
  5V: J3.5V, ATTiny85.VCC, DC_5V.pin2, R1.Pin_1, R2.Pin_0
  N5: ATTiny85.PB3(ADC3), S1.leg1, R1.Pin_0
  N6: ATTiny85.PB4(ADC2), S2.leg1, R2.Pin_1
  N7: K-.pin1, K-.pin5, R3.Pin_1, A+1.pin2, A+1.pin6
  N8: K-.pin2, K-.pin4, R5.Pin_1, A+1.pin1, A+1.pin3
  N9: K-.pin3, K-.pin6, R4.Pin_1, A+1.pin4, A+1.pin5

notes:
  GND
  Vcc
  MISO
  SCK
  Rev.4ds
  RESET
  ICSP
  (c) 2017 mra@coraxium.de
  Lichtprozessor 3X6
  MOSI
  A+
  K-
  +
  -

custom parts:
  Generic double row male header - 6 pins: Generic double row male header
